# Fritzing sketch wifi_signal_monitor (saved by Fritzing 0.9.3b)
breadboards: 1

parts:
  U1 = NodeMCU V1.0  # not connected
  LED1 = RGB LED (com. cathode, rgb) [package="5 mm [THT]"]
  R1 = Resistor [tolerance=±5% resistance=100 package=THT]
  R2 = Resistor [tolerance=±5% resistance=100 package=THT]
  R3 = Resistor [tolerance=±5% resistance=100 package=THT]

nets:
  N1: LED1.red_anode, R1.Pin_0
  N2: LED1.green_anode, R2.Pin_0
  N3: LED1.blue_anode, R3.Pin_0

custom parts:
  NodeMCU V1.0: ESP8266 based NodeMCU
